# Fritzing sketch 아두이노 rc카(1) (saved by Fritzing 0.8.7b)
breadboards: 1

parts:
  L298N1 = L298N DC motor driver
  M1 = DC Motor  # not connected
  M2 = DC Motor  # not connected
  M3 = DC Motor  # not connected
  M4 = DC Motor  # not connected
  부품2 = Arduino Uno (Rev3)

nets:
  N1: L298N1.ENA, 부품2.D10_PWM/SS
  N2: L298N1.ENB, 부품2.D11_PWM/MOSI
  N3: L298N1.IN1, 부품2.D5_PWM
  N4: L298N1.IN2, 부품2.D4
  N5: L298N1.IN3, 부품2.D3_PWM

custom parts:
  L298N DC motor driver: 2x DC motor driver with 78M05 positive voltage regulator (7..35 V) L298N: max 46 V, 2 A Set 5 V Enable jumper to enable 5 V regultor (needed for the L298N) and +5 V output at screw terminal or supply external +5 V at screw terminal Set ENA and/or ENB to +5 V to enable motor permanently or supply ENA and/or ENB with PWM signal IN1 and IN2 set rotation directory for motor A (OUT1/OUT2) IN2 and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
